// Logisim project PH1 CPU.circ as structural Verilog: 1 circuit, main circuit main
module main (
);

  wire and_1_out, and_2_out, and_3_out, and_4_out, and_5_out, and_6_out, and_7_out, and_8_out, and_9_out,
       and_10_out, and_11_out, and_12_out, and_13_out, and_14_out, and_15_out, and_16_out, and_17_out,
       and_18_out, and_19_out, and_20_out, and_21_out, and_22_out, and_23_out, and_24_out, and_25_out,
       and_26_out, and_27_out, clock_1_out, comparator_1_eq, comparator_1_gt, comparator_1_lt,
       decoder_1_out0, decoder_1_out1, decoder_1_out2, decoder_1_out3, decoder_1_out4, decoder_1_out5,
       decoder_1_out6, decoder_1_out7, decoder_2_out0, decoder_2_out1, decoder_2_out2, decoder_2_out3,
       decoder_2_out4, decoder_2_out5, decoder_2_out6, decoder_2_out7, decoder_2_out8, decoder_2_out9,
       decoder_2_out10, decoder_2_out11, decoder_2_out12, decoder_2_out13, decoder_2_out14, decoder_2_out15,
       nand_1_out, nor_1_out, nor_2_out, nor_3_out, nor_4_out, not_1_out, not_2_out, not_3_out, not_4_out,
       not_5_out, or_1_out, or_2_out, or_3_out, or_4_out, or_5_out, or_6_out, or_7_out, or_8_out, or_9_out,
       or_10_out, or_11_out, or_12_out, or_13_out, or_15_out;
  wire [2:0] counter_1_q;
  wire [3:0] bitselector_1_out, RI_q;
  wire [7:0] AC_q, adder_1_out, and_28_out, controlled_buffer_1_out, controlled_buffer_3_out,
       controlled_buffer_4_out, controlled_buffer_5_out, controlled_buffer_7_out, controlled_buffer_8_out,
       controlled_buffer_9_out, controlled_buffer_11_out, controlled_buffer_12_out, divider_1_out,
       multiplier_1_out, negator_1_out, or_14_out, PC_q, ram_1_data, RDM_q, REM_q, subtractor_1_out,
       xor_1_out;

  Clock clock_1 (.out(clock_1_out));
  and and_1 (and_1_out, clock_1_out, nand_1_out);
  Counter #(.width(3), .max('h7)) counter_1 (
    .count(and_1_out), .Q(counter_1_q), .clk(and_1_out));  // open: load, D, carry, clr
  nand nand_1 (nand_1_out, decoder_1_out3, decoder_2_out15);
  Decoder #(.select(3), .enable("false")) decoder_1 (
    .out0(decoder_1_out0), .out1(decoder_1_out1), .out2(decoder_1_out2), .out3(decoder_1_out3),
    .out4(decoder_1_out4), .out5(decoder_1_out5), .out6(decoder_1_out6), .out7(decoder_1_out7),
    .sel(counter_1_q));
  Decoder #(.select(4), .enable("false")) decoder_2 (
    .out0(decoder_2_out0), .out1(decoder_2_out1), .out2(decoder_2_out2), .out3(decoder_2_out3),
    .out4(decoder_2_out4), .out5(decoder_2_out5), .out6(decoder_2_out6), .out7(decoder_2_out7),
    .out8(decoder_2_out8), .out9(decoder_2_out9), .out10(decoder_2_out10), .out11(decoder_2_out11),
    .out12(decoder_2_out12), .out13(decoder_2_out13), .out14(decoder_2_out14), .out15(decoder_2_out15),
    .sel(RI_q));
  nor nor_1 (nor_1_out, decoder_2_out0, decoder_2_out7, decoder_2_out15);
  and and_2 (and_2_out, decoder_1_out7, decoder_2_out1);
  or or_1 (or_1_out, decoder_2_out3, decoder_2_out4, decoder_2_out5, decoder_2_out6, decoder_2_out8, decoder_2_out9, decoder_2_out10);
  or or_2 (or_2_out, decoder_2_out4, decoder_2_out6, decoder_2_out8, decoder_2_out10);
  or or_3 (or_3_out, decoder_2_out5, decoder_2_out6, decoder_2_out9, decoder_2_out10);
  or or_4 (or_4_out, decoder_2_out7, decoder_2_out8, decoder_2_out9, decoder_2_out10);
  nor nor_2 (nor_2_out, decoder_2_out0, decoder_2_out7, decoder_2_out15);
  nor nor_3 (nor_3_out, decoder_2_out12, decoder_2_out13, decoder_2_out14);
  or or_5 (or_5_out, decoder_2_out1, decoder_2_out3, decoder_2_out4, decoder_2_out5, decoder_2_out6, decoder_2_out8, decoder_2_out9, decoder_2_out10);
  and and_3 (and_3_out, decoder_1_out7, decoder_2_out2);
  and and_4 (and_4_out, decoder_1_out6, decoder_2_out2);
  or or_6 (or_6_out, decoder_2_out1, decoder_2_out3, decoder_2_out4, decoder_2_out5, decoder_2_out6, decoder_2_out8, decoder_2_out9, decoder_2_out10);
  and and_5 (and_5_out, decoder_1_out4, nor_1_out);
  and and_6 (and_6_out, nor_1_out, decoder_1_out3);
  and and_7 (and_7_out, decoder_1_out7, or_1_out);
  and and_8 (and_8_out, decoder_1_out3, decoder_2_out7);
  and and_9 (and_9_out, decoder_1_out6, decoder_2_out2);
  not not_1 (not_1_out, or_3_out);
  not not_2 (not_2_out, or_2_out);
  not not_3 (not_3_out, or_4_out);
  and and_10 (and_10_out, decoder_1_out3, nor_2_out);
  and and_11 (and_11_out, nor_2_out, decoder_1_out5, nor_3_out);
  and and_12 (and_12_out, nor_2_out, decoder_1_out4);
  and and_13 (and_13_out, decoder_1_out6, or_5_out);
  and and_14 (and_14_out, decoder_1_out5, nor_4_out);
  nor nor_4 (nor_4_out, decoder_2_out0, decoder_2_out7, decoder_2_out15, decoder_2_out11, decoder_2_out12, decoder_2_out13, decoder_2_out14);
  and and_15 (and_15_out, decoder_1_out7, or_6_out);
  Comparator comparator_1 (
    .a({8{1'b0}}), .b(controlled_buffer_7_out), .gt(comparator_1_gt), .eq(comparator_1_eq),
    .lt(comparator_1_lt));
  or or_7 (or_7_out, decoder_1_out1, and_5_out);
  or or_8 (or_8_out, and_6_out, decoder_1_out0);
  not not_4 (not_4_out, or_9_out);
  or or_9 (or_9_out, and_7_out, and_8_out);
  and and_16 (and_16_out, not_3_out, not_1_out, not_2_out);
  and and_17 (and_17_out, not_3_out, not_1_out, or_2_out);
  and and_18 (and_18_out, not_3_out, or_3_out, not_2_out);
  and and_19 (and_19_out, not_3_out, or_3_out, or_2_out);
  and and_20 (and_20_out, or_4_out, not_1_out, not_2_out);
  and and_21 (and_21_out, or_4_out, not_1_out, or_2_out);
  and and_22 (and_22_out, or_4_out, or_3_out, not_2_out);
  and and_23 (and_23_out, or_4_out, or_3_out, or_2_out);
  or or_10 (or_10_out, decoder_1_out0, and_10_out, and_11_out);
  or or_11 (or_11_out, decoder_1_out1, and_12_out, and_13_out);
  or or_12 (or_12_out, decoder_2_out11, and_24_out, and_25_out, and_26_out);
  and and_24 (and_24_out, decoder_2_out12, comparator_1_eq);
  and and_25 (and_25_out, decoder_2_out13, comparator_1_gt);
  and and_26 (and_26_out, decoder_2_out14, comparator_1_lt);
  BitSelector #(.group(4)) bitselector_1 (.in(controlled_buffer_3_out), .out(bitselector_1_out), .sel(and_1_out));
  Register #(.width(4), .trigger("high")) RI (
    .D(bitselector_1_out), .en(and_1_out), .Q(RI_q), .clk(and_1_out));  // open: clr
  assign controlled_buffer_1_out = and_2_out ? controlled_buffer_5_out : 8'bz;  // Controlled_Buffer controlled_buffer_1
  assign controlled_buffer_1_out = or_9_out ? controlled_buffer_12_out : 8'bz;  // Controlled_Buffer controlled_buffer_2
  or or_13 (or_13_out, decoder_1_out2, and_14_out, and_15_out, and_27_out);
  and and_27 (and_27_out, decoder_1_out5, or_12_out);
  assign controlled_buffer_3_out = decoder_1_out2 ? controlled_buffer_5_out : 8'bz;  // Controlled_Buffer controlled_buffer_3
  assign controlled_buffer_4_out = and_27_out ? controlled_buffer_5_out : 8'bz;  // Controlled_Buffer controlled_buffer_4
  Counter PC (.D(controlled_buffer_4_out), .count(or_7_out), .Q(PC_q), .clk(or_7_out));  // open: load, carry, clr
  assign controlled_buffer_5_out = or_8_out ? PC_q : 8'bz;  // Controlled_Buffer controlled_buffer_5
  Register #(.trigger("high")) AC (
    .D(controlled_buffer_1_out), .en(and_1_out), .Q(AC_q), .clk(and_1_out));  // open: clr
  assign controlled_buffer_5_out = and_9_out ? AC_q : 8'bz;  // Controlled_Buffer controlled_buffer_6
  assign controlled_buffer_7_out = not_4_out ? AC_q : 8'bz;  // Controlled_Buffer controlled_buffer_7
  assign controlled_buffer_8_out = and_4_out ? controlled_buffer_5_out : 8'bz;  // Controlled_Buffer controlled_buffer_8
  assign controlled_buffer_9_out = or_10_out ? controlled_buffer_5_out : 8'bz;  // Controlled_Buffer controlled_buffer_9
  Adder adder_1 (.a(controlled_buffer_5_out), .b(controlled_buffer_7_out), .out(adder_1_out));  // open: cin, cout
  Subtractor subtractor_1 (
    .a(controlled_buffer_5_out), .b(controlled_buffer_7_out), .out(subtractor_1_out));  // open: bin, bout
  Multiplier multiplier_1 (
    .a(controlled_buffer_5_out), .b(controlled_buffer_7_out), .out(multiplier_1_out));  // open: cin, cout
  Divider divider_1 (
    .a(controlled_buffer_5_out), .b(controlled_buffer_7_out), .out(divider_1_out));  // open: upper, rem
  Negator negator_1 (.in(controlled_buffer_7_out), .out(negator_1_out));
  assign and_28_out = controlled_buffer_5_out & controlled_buffer_7_out;  // AND_Gate and_28, 8 bits wide
  assign or_14_out = controlled_buffer_5_out | controlled_buffer_7_out;  // OR_Gate or_14, 8 bits wide
  assign xor_1_out = controlled_buffer_5_out ^ controlled_buffer_7_out;  // XOR_Gate xor_1, 8 bits wide
  Register #(.trigger("high")) RDM (
    .D(controlled_buffer_8_out), .en(and_1_out), .Q(RDM_q), .clk(and_1_out));  // open: clr
  assign controlled_buffer_5_out = or_13_out ? RDM_q : 8'bz;  // Controlled_Buffer controlled_buffer_10
  Register #(.trigger("high")) REM (
    .D(controlled_buffer_9_out), .en(and_1_out), .Q(REM_q), .clk(and_1_out));  // open: clr
  assign controlled_buffer_11_out = or_15_out ? REM_q : 8'bz;  // Controlled_Buffer controlled_buffer_11
  or or_15 (or_15_out, and_3_out, or_11_out);
  assign controlled_buffer_12_out = and_16_out ? adder_1_out : 8'bz;  // Controlled_Buffer controlled_buffer_12
  assign controlled_buffer_12_out = and_17_out ? subtractor_1_out : 8'bz;  // Controlled_Buffer controlled_buffer_13
  assign controlled_buffer_12_out = and_18_out ? multiplier_1_out : 8'bz;  // Controlled_Buffer controlled_buffer_14
  assign controlled_buffer_12_out = and_19_out ? divider_1_out : 8'bz;  // Controlled_Buffer controlled_buffer_15
  assign controlled_buffer_12_out = and_20_out ? negator_1_out : 8'bz;  // Controlled_Buffer controlled_buffer_16
  assign controlled_buffer_12_out = and_21_out ? and_28_out : 8'bz;  // Controlled_Buffer controlled_buffer_17
  assign controlled_buffer_12_out = and_22_out ? or_14_out : 8'bz;  // Controlled_Buffer controlled_buffer_18
  assign controlled_buffer_12_out = and_23_out ? xor_1_out : 8'bz;  // Controlled_Buffer controlled_buffer_19
  RAM ram_1 (.addr(controlled_buffer_11_out), .data(ram_1_data), .clk(and_1_out), .ld(not_5_out));  // open: sel, clr
  not not_5 (not_5_out, and_3_out);
  assign ram_1_data = and_3_out ? RDM_q : 8'bz;  // Controlled_Buffer controlled_buffer_20
  assign controlled_buffer_8_out = or_11_out ? ram_1_data : 8'bz;  // Controlled_Buffer controlled_buffer_21
endmodule
